// Logisim project proj_2_1_top.circ as structural Verilog: 9 circuits, main circuit testbench
module TOP (
  input  clk,
  input  rst,
  input  [31:0] inst,
  output [31:0] inst_addr,
  output mem_wen,
  output [31:0] mem_din,
  output [31:0] mem_dout,
  output [31:0] mem_addr,
  output control_en,
  output [31:0] control_pc,
  output wb_en,
  output [4:0] wb_addr,
  output [31:0] wb_data
);

  wire ASel, BSel, control_e, controller_1_op_add, controller_1_op_and, controller_1_op_lt,
       controller_1_op_ltu, controller_1_op_rs2_imm, controller_1_op_sra, controller_1_op_srl,
       instr_decoder_1_b_beq, instr_decoder_1_i_jalr, instr_decoder_1_i_type, instr_decoder_1_j_jal,
       instr_decoder_1_load, instr_decoder_1_r_type, instr_decoder_1_s_type, instr_decoder_1_u_auipc,
       instr_decoder_1_u_lui, mem_ren, mem_we, wb_e;
  wire [1:0] WBSel;
  wire [2:0] funct3;
  wire [4:0] addrD, instr_decoder_1_rs1, instr_decoder_1_rs2, wb_add;
  wire [31:0] A, adder_1_out, alu_res, and_1_out, B, control_p, imm, inst_add, mem_dou, multiplexer_1_out,
       multiplexer_11_out, multiplexer_12_out, wb_dat;

  Adder #(.width(32)) adder_1 (.a(inst_addr), .b(32'h4), .out(adder_1_out));  // open: cin, cout
  Register #(.width(32)) register_1 (.D(multiplexer_1_out), .clk(clk), .Q(inst_addr), .clr(rst));  // open: en
  Multiplexer #(.width(32)) multiplexer_1 (
    .in0(adder_1_out), .in1(control_p), .out(multiplexer_1_out), .sel(control_en));
  instr_decoder instr_decoder_1 (
    .inst(inst), .rd(addrD), .rs1(instr_decoder_1_rs1), .rs2(instr_decoder_1_rs2), .imm(imm),
    .funct3(funct3), .I_type(instr_decoder_1_i_type), .S_type(instr_decoder_1_s_type),
    .b_beq(instr_decoder_1_b_beq), .u_lui(instr_decoder_1_u_lui), .u_auipc(instr_decoder_1_u_auipc),
    .j_jal(instr_decoder_1_j_jal), .R_type(instr_decoder_1_r_type), .i_jalr(instr_decoder_1_i_jalr),
    .load(instr_decoder_1_load));  // open: opcode, funct7
  assign and_1_out = alu_res & 32'hfffffffe;  // AND_Gate and_1, 32 bits wide
  Multiplexer #(.width(32)) multiplexer_2 (
    .in0(alu_res), .in1(and_1_out), .out(control_p), .sel(instr_decoder_1_i_jalr));
  RegFile regfile_1 (
    .DataD(wb_dat), .clk(clk), .RegWEn(wb_e), .AddrD(addrD), .AddrA(instr_decoder_1_rs1),
    .AddrB(instr_decoder_1_rs2), .rst(rst), .DataA(A), .DataB(B));
  Multiplexer #(.width(5)) multiplexer_3 (.in0({5{1'b0}}), .in1(addrD), .out(wb_add), .sel(wb_e));
  Controller controller_1 (
    .inst(inst), .DataA(A), .DataB(B), .funct3(funct3), .b_beq(instr_decoder_1_b_beq),
    .i_jalr(instr_decoder_1_i_jalr), .j_jal(instr_decoder_1_j_jal), .I_type(instr_decoder_1_i_type),
    .u_auipc(instr_decoder_1_u_auipc), .R_type(instr_decoder_1_r_type), .load(instr_decoder_1_load),
    .S_type(instr_decoder_1_s_type), .u_lui(instr_decoder_1_u_lui), .mem_ren(mem_ren), .mem_wen(mem_we),
    .control_en(control_e), .wb_en(wb_e), .A_sel(ASel), .B_sel(BSel), .wb_src(WBSel),
    .op_sra(controller_1_op_sra), .op_srl(controller_1_op_srl), .op_lt(controller_1_op_lt),
    .op_ltu(controller_1_op_ltu), .op_add(controller_1_op_add), .op_and(controller_1_op_and),
    .op_rs2_imm(controller_1_op_rs2_imm));
  Multiplexer #(.width(32)) multiplexer_4 (.in0(inst_add), .in1({32{1'b0}}), .out(inst_addr), .sel(rst));
  Multiplexer multiplexer_5 (.in0(mem_we), .in1(1'b0), .out(mem_wen), .sel(rst));
  Multiplexer #(.width(5)) multiplexer_6 (.in0(wb_add), .in1({5{1'b0}}), .out(wb_addr), .sel(rst));
  Multiplexer #(.select(2), .width(32)) multiplexer_7 (
    .in0(alu_res), .in1(mem_dou), .in2(adder_1_out), .out(wb_dat), .sel(WBSel));  // open: in3
  ALU alu_1 (
    .rsa(multiplexer_11_out), .rsb_imm(multiplexer_12_out), .op_add(controller_1_op_add),
    .op_lt(controller_1_op_lt), .op_ltu(controller_1_op_ltu), .op_and(controller_1_op_and),
    .op_srl(controller_1_op_srl), .op_sra(controller_1_op_sra), .op_rs2_imm(controller_1_op_rs2_imm),
    .dout(alu_res));  // open: op_eq, op_equ
  Multiplexer #(.width(32)) multiplexer_8 (.in0(wb_dat), .in1({32{1'b0}}), .out(wb_data), .sel(rst));
  Multiplexer #(.width(32)) multiplexer_9 (.in0(B), .in1({32{1'b0}}), .out(mem_din), .sel(rst));
  Multiplexer #(.width(32)) multiplexer_10 (.in0(mem_dou), .in1({32{1'b0}}), .out(mem_dout), .sel(rst));
  Multiplexer #(.width(32)) multiplexer_11 (.in0(A), .in1(inst_addr), .out(multiplexer_11_out), .sel(ASel));
  Multiplexer #(.width(32)) multiplexer_12 (.in0(B), .in1(imm), .out(multiplexer_12_out), .sel(BSel));
  Multiplexer multiplexer_13 (.in0(control_e), .in1(1'b0), .out(control_en), .sel(rst));
  Memory memory_1 (
    .alu_res(alu_res), .mem_wen(mem_wen), .mem_ren(mem_ren), .clk(clk), .mem_din(B), .funct3(funct3),
    .mem_dout(mem_dou));
  Multiplexer #(.width(32)) multiplexer_14 (.in0(alu_res), .in1({32{1'b0}}), .out(mem_addr), .sel(rst));
  Multiplexer multiplexer_15 (.in0(wb_e), .in1(1'b0), .out(wb_en), .sel(rst));
  Multiplexer #(.width(32)) multiplexer_16 (.in0(control_p), .in1({32{1'b0}}), .out(control_pc), .sel(rst));

  // Other names for the same wires on the sheet: current_pc[31:0] = inst_addr; mem_add[31:0] = alu_res;
  //   mem_di[31:0] = B

  // Notes on the sheet:
  //   DON'T TOUCH!
endmodule

module testbench (
  input  rst,
  output [5:0] out_2,
  output out_3,
  output halt,
  output [31:0] out_5,
  output [31:0] mem_dout,
  output [31:0] mem_addr,
  output out_8,
  output [31:0] out_9,
  output out_10,
  output [4:0] out_11,
  output [31:0] out_12
);

  wire and_1_out, carry, clk, not_1_out, not_2_out, por_1_out, rst_t;
  wire [31:0] inst, inst_addr;

  not not_1 (not_1_out, inst[2]);
  not not_2 (not_2_out, inst[3]);
  POR por_1 (.out(por_1_out));
  TOP top_1 (
    .clk(clk), .rst(rst_t), .inst(inst), .inst_addr(inst_addr), .mem_wen(out_3), .mem_din(out_5),
    .mem_dout(mem_dout), .mem_addr(mem_addr), .control_en(out_8), .control_pc(out_9), .wb_en(out_10),
    .wb_addr(out_11), .wb_data(out_12));
  Clock clock_1 (.out(clk));
  or or_1 (rst_t, rst, por_1_out);
  and and_1 (and_1_out, inst[0], inst[1], not_1_out, not_2_out, inst[4], inst[5], inst[6]);
  or or_2 (halt, and_1_out, carry);
  Counter #(.max('h3f), .width(6)) counter_1 (
    .clr(rst_t), .up(1'b1), .count(1'b1), .clk(clk), .carry(carry), .Q(out_2));  // open: load, D
  // ROM #(.line("quad"), .misaligned("true")) inst_mem: pin names not known; wires that end beside it: inst_addr[7:0], inst[7:0], inst[15:8], inst[23:16], inst[31:24]
  // Probe on inst

  // Other names for the same wires on the sheet: control_en = out_8; control_pc[31:0] = out_9; mem_din[31:0] = out_5;
  //   mem_wen = out_3; wb_addr[4:0] = out_11; wb_data[31:0] = out_12; wb_en = out_10

  // Notes on the sheet:
  //   DON'T TOUCH!
  //   contents of inst_mem (hex, n*v repeats v):
  //   7b 0 0 93 0 10 10 23 0 10 11 23 0 10 21 3 0 21 1 63 51 b7
  //   you can write any instruction in
endmodule

module RegFile (
  input  [31:0] DataD,
  input  clk,
  input  RegWEn,
  input  [4:0] AddrD,
  input  [4:0] AddrA,
  input  [4:0] AddrB,
  input  rst,
  output [31:0] DataA,
  output [31:0] DataB
);

  wire AddrD_x0, AddrD_x1, AddrD_x2, AddrD_x3, AddrD_x4, AddrD_x5, AddrD_x6, AddrD_x7, AddrD_x8, AddrD_x9,
       AddrD_x10, AddrD_x11, AddrD_x12, AddrD_x13, AddrD_x14, AddrD_x15, AddrD_x16, AddrD_x17, AddrD_x18,
       AddrD_x19, AddrD_x20, AddrD_x21, AddrD_x22, AddrD_x23, AddrD_x24, AddrD_x25, AddrD_x26, AddrD_x27,
       AddrD_x28, AddrD_x29, AddrD_x30, AddrD_x31;
  wire [31:0] Data_x0, Data_x1, Data_x2, Data_x3, Data_x4, Data_x5, Data_x6, Data_x7, Data_x8, Data_x9,
       Data_x10, Data_x11, Data_x12, Data_x13, Data_x14, Data_x15, Data_x16, Data_x17, Data_x18, Data_x19,
       Data_x20, Data_x21, Data_x22, Data_x23, Data_x24, Data_x25, Data_x26, Data_x27, Data_x28, Data_x29,
       Data_x30, Data_x31;

  Demultiplexer #(.select(5)) demultiplexer_1 (
    .out0(AddrD_x0), .out1(AddrD_x1), .out2(AddrD_x2), .out3(AddrD_x3), .out4(AddrD_x4), .out5(AddrD_x5),
    .out6(AddrD_x6), .out7(AddrD_x7), .out8(AddrD_x8), .out9(AddrD_x9), .out10(AddrD_x10), .out11(AddrD_x11),
    .out12(AddrD_x12), .out13(AddrD_x13), .out14(AddrD_x14), .out15(AddrD_x15), .out16(AddrD_x16),
    .out17(AddrD_x17), .out18(AddrD_x18), .out19(AddrD_x19), .out20(AddrD_x20), .out21(AddrD_x21),
    .out22(AddrD_x22), .out23(AddrD_x23), .out24(AddrD_x24), .out25(AddrD_x25), .out26(AddrD_x26),
    .out27(AddrD_x27), .out28(AddrD_x28), .out29(AddrD_x29), .out30(AddrD_x30), .out31(AddrD_x31),
    .in(RegWEn), .sel(AddrD));
  Register #(.width(32)) x0 (.D(DataD), .en(AddrD_x0), .clk(clk), .Q(Data_x0), .clr(rst));
  Register #(.width(32)) x1 (.D(DataD), .en(AddrD_x1), .clk(clk), .Q(Data_x1), .clr(rst));
  Register #(.width(32)) x2 (.D(DataD), .en(AddrD_x2), .clk(clk), .Q(Data_x2), .clr(rst));
  Register #(.width(32)) x3 (.D(DataD), .en(AddrD_x3), .clk(clk), .Q(Data_x3), .clr(rst));
  Register #(.width(32)) x4 (.D(DataD), .en(AddrD_x4), .clk(clk), .Q(Data_x4), .clr(rst));
  Register #(.width(32)) x5 (.D(DataD), .en(AddrD_x5), .clk(clk), .Q(Data_x5), .clr(rst));
  Register #(.width(32)) x6 (.D(DataD), .en(AddrD_x6), .clk(clk), .Q(Data_x6), .clr(rst));
  Register #(.width(32)) x7 (.D(DataD), .en(AddrD_x7), .clk(clk), .Q(Data_x7), .clr(rst));
  Register #(.width(32)) x8 (.D(DataD), .en(AddrD_x8), .clk(clk), .Q(Data_x8), .clr(rst));
  Register #(.width(32)) x9 (.D(DataD), .en(AddrD_x9), .clk(clk), .Q(Data_x9), .clr(rst));
  Register #(.width(32)) x10 (.D(DataD), .en(AddrD_x10), .clk(clk), .Q(Data_x10), .clr(rst));
  Register #(.width(32)) x11 (.D(DataD), .en(AddrD_x11), .clk(clk), .Q(Data_x11), .clr(rst));
  Register #(.width(32)) x12 (.D(DataD), .en(AddrD_x12), .clk(clk), .Q(Data_x12), .clr(rst));
  Register #(.width(32)) x13 (.D(DataD), .en(AddrD_x13), .clk(clk), .Q(Data_x13), .clr(rst));
  Register #(.width(32)) x14 (.D(DataD), .en(AddrD_x14), .clk(clk), .Q(Data_x14), .clr(rst));
  Register #(.width(32)) x15 (.D(DataD), .en(AddrD_x15), .clk(clk), .Q(Data_x15), .clr(rst));
  Register #(.width(32)) x16 (.D(DataD), .en(AddrD_x16), .clk(clk), .Q(Data_x16), .clr(rst));
  Register #(.width(32)) x17 (.D(DataD), .en(AddrD_x17), .clk(clk), .Q(Data_x17), .clr(rst));
  Register #(.width(32)) x18 (.D(DataD), .en(AddrD_x18), .clk(clk), .Q(Data_x18), .clr(rst));
  Register #(.width(32)) x19 (.D(DataD), .en(AddrD_x19), .clk(clk), .Q(Data_x19), .clr(rst));
  Register #(.width(32)) x20 (.D(DataD), .en(AddrD_x20), .clk(clk), .Q(Data_x20), .clr(rst));
  Register #(.width(32)) x21 (.D(DataD), .en(AddrD_x21), .clk(clk), .Q(Data_x21), .clr(rst));
  Register #(.width(32)) x22 (.D(DataD), .en(AddrD_x22), .clk(clk), .Q(Data_x22), .clr(rst));
  Register #(.width(32)) x23 (.D(DataD), .en(AddrD_x23), .clk(clk), .Q(Data_x23), .clr(rst));
  Register #(.width(32)) x24 (.D(DataD), .en(AddrD_x24), .clk(clk), .Q(Data_x24), .clr(rst));
  Register #(.width(32)) x25 (.D(DataD), .en(AddrD_x25), .clk(clk), .Q(Data_x25), .clr(rst));
  Register #(.width(32)) x26 (.D(DataD), .en(AddrD_x26), .clk(clk), .Q(Data_x26), .clr(rst));
  Register #(.width(32)) x27 (.D(DataD), .en(AddrD_x27), .clk(clk), .Q(Data_x27), .clr(rst));
  Register #(.width(32)) x28 (.D(DataD), .en(AddrD_x28), .clk(clk), .Q(Data_x28), .clr(rst));
  Register #(.width(32)) x29 (.D(DataD), .en(AddrD_x29), .clk(clk), .Q(Data_x29), .clr(rst));
  Register #(.width(32)) x30 (.D(DataD), .en(AddrD_x30), .clk(clk), .Q(Data_x30), .clr(rst));
  Register #(.width(32)) x31 (.D(DataD), .en(AddrD_x31), .clk(clk), .Q(Data_x31), .clr(rst));
  Multiplexer #(.select(5), .width(32)) multiplexer_1 (
    .in0(Data_x0), .in1(Data_x1), .in2(Data_x2), .in3(Data_x3), .in4(Data_x4), .in5(Data_x5), .in6(Data_x6),
    .in7(Data_x7), .in8(Data_x8), .in9(Data_x9), .in10(Data_x10), .in11(Data_x11), .in12(Data_x12),
    .in13(Data_x13), .in14(Data_x14), .in15(Data_x15), .in16(Data_x16), .in17(Data_x17), .in18(Data_x18),
    .in19(Data_x19), .in20(Data_x20), .in21(Data_x21), .in22(Data_x22), .in23(Data_x23), .in24(Data_x24),
    .in25(Data_x25), .in26(Data_x26), .in27(Data_x27), .in28(Data_x28), .in29(Data_x29), .in30(Data_x30),
    .in31(Data_x31), .out(DataA), .sel(AddrA));
  Multiplexer #(.select(5), .width(32)) multiplexer_2 (
    .in0(Data_x0), .in1(Data_x1), .in2(Data_x2), .in3(Data_x3), .in4(Data_x4), .in5(Data_x5), .in6(Data_x6),
    .in7(Data_x7), .in8(Data_x8), .in9(Data_x9), .in10(Data_x10), .in11(Data_x11), .in12(Data_x12),
    .in13(Data_x13), .in14(Data_x14), .in15(Data_x15), .in16(Data_x16), .in17(Data_x17), .in18(Data_x18),
    .in19(Data_x19), .in20(Data_x20), .in21(Data_x21), .in22(Data_x22), .in23(Data_x23), .in24(Data_x24),
    .in25(Data_x25), .in26(Data_x26), .in27(Data_x27), .in28(Data_x28), .in29(Data_x29), .in30(Data_x30),
    .in31(Data_x31), .out(DataB), .sel(AddrB));
endmodule

module ALU (
  input  [31:0] rsa,
  input  [31:0] rsb_imm,
  input  op_add,
  input  op_eq,
  input  op_lt,
  input  op_equ,
  input  op_ltu,
  input  op_and,
  input  op_srl,
  input  op_sra,
  input  op_rs2_imm,
  output [31:0] dout
);

  wire comparator_1_eq, comparator_1_gt, comparator_1_lt, comparator_2_eq, comparator_2_lt,
       multiplexer_1_out, multiplexer_2_out, multiplexer_3_out, multiplexer_4_out, or_1_out;
  wire [31:0] adder_1_out, and_1_out, bit_extender_1_out, multiplexer_5_out, multiplexer_6_out,
       multiplexer_7_out, multiplexer_8_out, shifter_1_out, shifter_2_out;

  // Probe on op_add
  Adder #(.width(32)) adder_1 (.a(rsa), .b(rsb_imm), .out(adder_1_out));  // open: cin, cout
  assign and_1_out = rsa & rsb_imm;  // AND_Gate and_1, 32 bits wide
  Shifter #(.shift("lr"), .width(32)) shifter_1 (.in(rsa), .\dist (rsb_imm[4:0]), .out(shifter_1_out));
  Shifter #(.shift("ar"), .width(32)) shifter_2 (.in(rsa), .\dist (rsb_imm[4:0]), .out(shifter_2_out));
  Comparator #(.width(32)) comparator_1 (
    .a(rsa), .b(rsb_imm), .gt(comparator_1_gt), .eq(comparator_1_eq), .lt(comparator_1_lt));
  Comparator #(.mode("unsigned"), .width(32)) comparator_2 (
    .a(rsa), .b(rsb_imm), .eq(comparator_2_eq), .lt(comparator_2_lt));  // open: gt
  Multiplexer multiplexer_1 (.in0(comparator_1_gt), .in1(comparator_1_eq), .out(multiplexer_1_out), .sel(op_eq));
  Multiplexer multiplexer_2 (.in0(multiplexer_1_out), .in1(comparator_1_lt), .out(multiplexer_2_out), .sel(op_lt));
  Multiplexer multiplexer_3 (.in0(multiplexer_2_out), .in1(comparator_2_eq), .out(multiplexer_3_out), .sel(op_equ));
  assign bit_extender_1_out = {{31{1'b0}}, multiplexer_4_out};  // Bit_Extender bit_extender_1
  Multiplexer multiplexer_4 (.in0(multiplexer_3_out), .in1(comparator_2_lt), .out(multiplexer_4_out), .sel(op_ltu));
  or or_1 (or_1_out, op_eq, op_ltu, op_lt, op_equ);
  Multiplexer #(.width(32)) multiplexer_5 (.in0(adder_1_out), .in1(and_1_out), .out(multiplexer_5_out), .sel(op_and));
  Multiplexer #(.width(32)) multiplexer_6 (
    .in0(multiplexer_5_out), .in1(shifter_1_out), .out(multiplexer_6_out), .sel(op_srl));
  Multiplexer #(.width(32)) multiplexer_7 (
    .in0(multiplexer_6_out), .in1(shifter_2_out), .out(multiplexer_7_out), .sel(op_sra));
  Multiplexer #(.width(32)) multiplexer_8 (
    .in0(multiplexer_7_out), .in1(bit_extender_1_out), .out(multiplexer_8_out), .sel(or_1_out));
  Multiplexer #(.width(32)) multiplexer_9 (.in0(multiplexer_8_out), .in1(rsb_imm), .out(dout), .sel(op_rs2_imm));

  // Notes on the sheet:
  //   unsigned
endmodule

module imm_gen (
  input  [31:0] inst,
  output [31:0] I_imm,
  output [31:0] S_imm,
  output [31:0] B_imm,
  output [31:0] U_imm,
  output [31:0] J_imm
);

  // NoConnect on inst[6:0]
  assign {I_imm[31], B_imm[31:12]} = {{20{inst[31]}}, inst[31]};  // Bit_Extender bit_extender_1
  // NoConnect on I_imm[31]
  // NoConnect on {I_imm[31], B_imm[31:13]}
  // NoConnect on {I_imm[31], B_imm[31:24]}

  assign B_imm[11:0] = {inst[7], inst[30:25], inst[11:8], 1'b0};
  assign I_imm[30:0] = {B_imm[31:12], inst[30:20]};
  assign J_imm = {B_imm[23:12], inst[19:12], inst[20], inst[30:21], 1'b0};
  assign S_imm = {I_imm[31], B_imm[31:12], inst[30:25], inst[11:7]};
  assign U_imm = {B_imm[12], inst[30:12], {12{1'b0}}};

  // Notes on the sheet:
  //   I-imm
  //   S-imm
  //   B-imm
  //   U-imm
  //   J-imm
endmodule

module instr_decoder (
  input  [31:0] inst,
  output [6:0] opcode,
  output [4:0] rd,
  output [4:0] rs1,
  output [4:0] rs2,
  output [31:0] imm,
  output [2:0] funct3,
  output [6:0] funct7,
  output I_type,
  output S_type,
  output b_beq,
  output u_lui,
  output u_auipc,
  output j_jal,
  output R_type,
  output i_jalr,
  output load
);

  wire or_1_out, or_2_out, or_3_out;
  wire [31:0] imm_gen_1_b_imm, imm_gen_1_i_imm, imm_gen_1_j_imm, imm_gen_1_s_imm, imm_gen_1_u_imm,
       multiplexer_1_out, multiplexer_2_out, multiplexer_3_out, multiplexer_4_out;

  // Probe on inst
  Comparator #(.width(7)) comparator_1 (.a(inst[6:0]), .b(7'b0010011), .eq(I_type));  // open: gt, lt
  Comparator #(.width(7)) comparator_2 (.a(inst[6:0]), .b(7'b0100011), .eq(S_type));  // open: gt, lt
  Comparator #(.width(7)) comparator_3 (.a(inst[6:0]), .b(7'b1100011), .eq(b_beq));  // open: gt, lt
  Comparator #(.width(7)) comparator_4 (.a(inst[6:0]), .b(7'b0110111), .eq(u_lui));  // open: gt, lt
  Comparator #(.width(7)) comparator_5 (.a(inst[6:0]), .b(7'b0010111), .eq(u_auipc));  // open: gt, lt
  Comparator #(.width(7)) comparator_6 (.a(inst[6:0]), .b(7'b1101111), .eq(j_jal));  // open: gt, lt
  Comparator #(.width(7)) comparator_7 (.a(inst[6:0]), .b(7'b0110011), .eq(R_type));  // open: gt, lt
  Comparator #(.width(7)) comparator_8 (.a(inst[6:0]), .b(7'b1100111), .eq(i_jalr));  // open: gt, lt
  Comparator #(.width(7)) comparator_9 (.a(inst[6:0]), .b(7'b0000011), .eq(load));  // open: gt, lt
  imm_gen imm_gen_1 (
    .inst(inst), .I_imm(imm_gen_1_i_imm), .S_imm(imm_gen_1_s_imm), .B_imm(imm_gen_1_b_imm),
    .U_imm(imm_gen_1_u_imm), .J_imm(imm_gen_1_j_imm));
  or or_1 (or_1_out, u_lui, u_auipc);
  or or_2 (or_2_out, i_jalr, load);
  Multiplexer #(.width(32)) multiplexer_1 (
    .in0({32{1'b0}}), .in1(imm_gen_1_i_imm), .out(multiplexer_1_out), .sel(or_3_out));
  or or_3 (or_3_out, I_type, or_2_out);
  Multiplexer #(.width(32)) multiplexer_2 (
    .in0(multiplexer_1_out), .in1(imm_gen_1_s_imm), .out(multiplexer_2_out), .sel(S_type));
  Multiplexer #(.width(32)) multiplexer_3 (
    .in0(multiplexer_2_out), .in1(imm_gen_1_b_imm), .out(multiplexer_3_out), .sel(b_beq));
  Multiplexer #(.width(32)) multiplexer_4 (
    .in0(multiplexer_3_out), .in1(imm_gen_1_u_imm), .out(multiplexer_4_out), .sel(or_1_out));
  Multiplexer #(.width(32)) multiplexer_5 (.in0(multiplexer_4_out), .in1(imm_gen_1_j_imm), .out(imm), .sel(j_jal));

  assign funct3 = inst[14:12];
  assign funct7 = inst[31:25];
  assign opcode = inst[6:0];
  assign rd = inst[11:7];
  assign rs1 = inst[19:15];
  assign rs2 = inst[24:20];
endmodule

module Controller (
  input  [31:0] inst,
  input  [31:0] DataA,
  input  [31:0] DataB,
  input  [2:0] funct3,
  input  b_beq,
  input  i_jalr,
  input  j_jal,
  input  I_type,
  input  u_auipc,
  input  R_type,
  input  load,
  input  S_type,
  input  u_lui,
  output mem_ren,
  output mem_wen,
  output control_en,
  output wb_en,
  output A_sel,
  output B_sel,
  output [1:0] wb_src,
  output op_sra,
  output op_srl,
  output op_lt,
  output op_ltu,
  output op_add,
  output op_and,
  output op_rs2_imm
);

  wire and_4_out, comparator_1_eq, comparator_2_eq, comparator_3_eq, comparator_4_eq, comparator_5_eq,
       comparator_7_eq, comparator_8_eq, comparator_9_eq, comparator_10_eq, comparator_11_eq,
       comparator_12_eq, comparator_13_eq, i_addi, i_lh, i_lw, r_add, s_sh, s_sw;
  wire [1:0] or_7_out;
  wire [6:0] funct7;

  Comparator #(.width(3)) comparator_1 (.a(funct3), .b(3'b011), .eq(comparator_1_eq));  // open: gt, lt
  and and_1 (op_ltu, comparator_1_eq, I_type);
  Comparator #(.width(3)) comparator_2 (.a(funct3), .b(3'b001), .eq(comparator_2_eq));  // open: gt, lt
  Comparator #(.width(3)) comparator_3 (.a(funct3), .b(3'b010), .eq(comparator_3_eq));  // open: gt, lt
  Comparator #(.width(32)) comparator_4 (.a(DataB), .b(DataA), .eq(comparator_4_eq));  // open: gt, lt
  and and_2 (i_lh, comparator_2_eq, load);
  and and_3 (i_lw, comparator_3_eq, load);
  Comparator #(.width(3)) comparator_5 (.a(funct3), .b(3'b000), .eq(comparator_5_eq));  // open: gt, lt
  Comparator #(.width(7)) comparator_6 (.a(funct7));  // open: b, gt, eq, lt
  Comparator #(.width(3)) comparator_7 (.a(funct3), .b(3'b010), .eq(comparator_7_eq));  // open: gt, lt
  or or_1 (op_add, r_add, i_addi, i_lw, i_lh, i_jalr, u_auipc, s_sw, s_sh, j_jal);
  and and_4 (and_4_out, comparator_4_eq, b_beq);
  and and_5 (r_add, comparator_5_eq, R_type);
  and and_6 (s_sw, comparator_7_eq, S_type);
  or or_2 (control_en, and_4_out, i_jalr, j_jal);
  or or_3 (wb_en, i_jalr, j_jal, I_type, u_auipc, u_lui, R_type, load);
  Comparator #(.width(3)) comparator_8 (.a(funct3), .b(3'b000), .eq(comparator_8_eq));  // open: gt, lt
  and and_7 (i_addi, comparator_8_eq, I_type);
  Comparator #(.width(3)) comparator_9 (.a(funct3), .b(3'b101), .eq(comparator_9_eq));  // open: gt, lt
  Comparator #(.width(3)) comparator_10 (.a(funct3), .b(3'b001), .eq(comparator_10_eq));  // open: gt, lt
  or or_4 (A_sel, u_auipc, u_lui, b_beq, j_jal);
  and and_8 (op_sra, comparator_9_eq, R_type);
  and and_9 (s_sh, comparator_10_eq, S_type);
  Comparator #(.width(3)) comparator_11 (.a(funct3), .b(3'b101), .eq(comparator_11_eq));  // open: gt, lt
  and and_10 (op_srl, comparator_11_eq, I_type);
  // Probe on B_sel
  or or_5 (B_sel, A_sel, op_ltu, i_jalr, i_addi, op_srl, op_and, i_lh, i_lw, s_sw, s_sh);
  Comparator #(.width(3)) comparator_12 (.a(funct3), .b(3'b010), .eq(comparator_12_eq));  // open: gt, lt
  and and_11 (op_lt, comparator_12_eq, R_type);
  Comparator #(.width(3)) comparator_13 (.a(funct3), .b(3'b111), .eq(comparator_13_eq));  // open: gt, lt
  or or_6 (or_7_out[1], i_jalr, j_jal);
  and and_12 (op_and, comparator_13_eq, I_type);
  Multiplexer #(.select(2), .width(2)) multiplexer_1 (
    .in0(2'b00), .in1(2'b01), .in2(2'b10), .out(wb_src), .sel(or_7_out));  // open: in3
  or or_7 (or_7_out[0], i_lh, i_lw);
  // Probe on wb_src

  assign mem_ren = load;
  assign mem_wen = S_type;
  assign op_rs2_imm = u_lui;

  // Other names for the same wires on the sheet: i_andi = op_and; i_sltiu = op_ltu; i_srli = op_srl; r_slt = op_lt;
  //   r_sra = op_sra

  // Notes on the sheet:
  //   PC_sel
  //   RegWen
endmodule

module Memory (
  input  [31:0] alu_res,
  input  mem_wen,
  input  mem_ren,
  input  clk,
  input  [31:0] mem_din,
  input  [2:0] funct3,
  output [31:0] mem_dout
);

  wire and_1_out, and_2_out, and_3_out, and_7_out, and_8_out, and_9_out, and_10_out, and_14_out, and_16_out,
       and_18_out, and_19_out, and_20_out, and_21_out, is_b, is_h, is_w, mem_wen_0, mem_wen_1, mem_wen_2,
       mem_wen_3, nor_1_out, nor_2_out, nor_3_out, not_1_out, not_2_out, not_3_out, not_4_out, not_5_out,
       not_6_out, not_7_out, not_8_out, or_1_out, or_2_out, or_3_out, or_4_out, or_5_out, or_6_out, or_7_out,
       or_8_out, or_9_out;
  wire [7:0] mem_dout_0, mem_dout_1, mem_dout_2, mem_dout_3;
  wire [15:0] addr_align, addr_alignoffset, multiplexer_1_out, multiplexer_2_out, multiplexer_3_out,
       multiplexer_4_out, multiplexer_5_out;
  wire [31:0] bit_extender_1_out, mem_din_new, mem_do, multiplexer_6_out, multiplexer_7_out,
       multiplexer_8_out, multiplexer_11_out, multiplexer_12_out;

  Multiplexer #(.width(16)) multiplexer_1 (
    .in0(addr_alignoffset), .in1(alu_res[15:0]), .out(multiplexer_1_out), .sel(nor_1_out));
  nor nor_1 (nor_1_out, alu_res[0], alu_res[1]);
  Multiplexer #(.width(16)) multiplexer_2 (
    .in0(alu_res[15:0]), .in1(addr_align), .out(multiplexer_2_out), .sel(alu_res[0]));
  Multiplexer #(.width(16)) multiplexer_3 (
    .in0(alu_res[15:0]), .in1(addr_align), .out(multiplexer_3_out), .sel(or_1_out));
  or or_1 (or_1_out, alu_res[0], alu_res[1]);
  and and_1 (and_1_out, alu_res[0], alu_res[1]);
  Multiplexer #(.width(16)) multiplexer_4 (
    .in0(multiplexer_2_out), .in1(addr_alignoffset), .out(multiplexer_4_out), .sel(alu_res[1]));
  Multiplexer #(.width(16)) multiplexer_5 (
    .in0(multiplexer_3_out), .in1(addr_alignoffset), .out(multiplexer_5_out), .sel(and_1_out));
  nor nor_2 (nor_2_out, alu_res[0], alu_res[1]);
  not not_1 (not_1_out, alu_res[1]);
  RAM #(.addrWidth(16), .asyncread("true"), .clearpin("true")) ram_1 (
    .addr(multiplexer_1_out), .we(mem_wen_0), .oe(mem_ren), .clk(clk), .din(mem_din_new[7:0]),
    .dout(mem_dout_0));  // open: clr
  RAM #(.addrWidth(16), .asyncread("true"), .clearpin("true")) ram_2 (
    .addr(multiplexer_4_out), .we(mem_wen_1), .oe(mem_ren), .clk(clk), .din(mem_din_new[15:8]),
    .dout(mem_dout_1));  // open: clr
  RAM #(.addrWidth(16), .asyncread("true"), .clearpin("true")) ram_3 (
    .addr(multiplexer_5_out), .we(mem_wen_2), .oe(mem_ren), .clk(clk), .din(mem_din_new[23:16]),
    .dout(mem_dout_2));  // open: clr
  RAM #(.addrWidth(16), .asyncread("true"), .clearpin("true")) ram_4 (
    .addr(addr_align), .we(mem_wen_3), .oe(mem_ren), .clk(clk), .din(mem_din_new[31:24]), .dout(mem_dout_3));  // open: clr
  or or_2 (or_2_out, nor_2_out, and_2_out);
  and and_2 (and_2_out, alu_res[0], alu_res[1]);
  nor nor_3 (nor_3_out, alu_res[0], alu_res[1]);
  and and_3 (and_3_out, alu_res[0], not_1_out);
  or or_3 (or_3_out, nor_3_out, and_3_out);
  or or_4 (or_4_out, or_2_out, is_w);
  and and_4 (mem_wen_0, mem_wen, or_4_out);
  or or_5 (or_5_out, or_3_out, is_w);
  and and_5 (mem_wen_1, mem_wen, or_5_out);
  assign addr_align = alu_res[15:0] & 16'hfffc;  // AND_Gate and_6, 16 bits wide
  not not_2 (not_2_out, alu_res[0]);
  and and_7 (and_7_out, alu_res[1], not_2_out);
  not not_3 (not_3_out, alu_res[1]);
  not not_4 (not_4_out, alu_res[0]);
  and and_8 (and_8_out, alu_res[0], not_3_out);
  and and_9 (and_9_out, alu_res[1], not_4_out);
  not not_5 (not_5_out, alu_res[1]);
  or or_6 (or_6_out, and_7_out, and_8_out);
  and and_10 (and_10_out, alu_res[0], alu_res[1]);
  and and_11 (is_b, ~funct3[0], ~funct3[1]);  // AND_Gate
  and and_12 (is_h, funct3[0], ~funct3[1]);  // AND_Gate
  and and_13 (is_w, ~funct3[0], funct3[1]);  // AND_Gate
  and and_14 (and_14_out, alu_res[0], not_5_out);
  or or_7 (or_7_out, and_9_out, and_10_out);
  Multiplexer #(.width(32)) multiplexer_6 (
    .in0({mem_dout_3, mem_dout_2, mem_dout_1, mem_dout_0}),
    .in1({mem_dout_0, mem_dout_3, mem_dout_2, mem_dout_1}), .out(multiplexer_6_out), .sel(and_14_out));
  or or_8 (or_8_out, or_6_out, is_w);
  and and_15 (mem_wen_2, mem_wen, or_8_out);
  or or_9 (or_9_out, or_7_out, is_w);
  and and_16 (and_16_out, alu_res[1], not_6_out);
  not not_6 (not_6_out, alu_res[0]);
  and and_17 (mem_wen_3, mem_wen, or_9_out);
  Adder #(.width(16)) adder_1 (.a(addr_align), .b(16'h4), .out(addr_alignoffset));  // open: cin, cout
  Multiplexer #(.width(32)) multiplexer_7 (.in0({32{1'b0}}), .in1(mem_do), .out(multiplexer_7_out), .sel(mem_ren));
  Multiplexer #(.width(32)) multiplexer_8 (
    .in0(multiplexer_6_out), .in1({mem_dout_1, mem_dout_0, mem_dout_3, mem_dout_2}), .out(multiplexer_8_out),
    .sel(and_16_out));
  assign bit_extender_1_out = {{16{multiplexer_7_out[15]}}, multiplexer_7_out[15:0]};  // Bit_Extender bit_extender_1
  Multiplexer #(.width(32)) multiplexer_9 (
    .in0(multiplexer_7_out), .in1(bit_extender_1_out), .out(mem_dout), .sel(is_h));
  and and_18 (and_18_out, alu_res[1], alu_res[0]);
  Multiplexer #(.width(32)) multiplexer_10 (
    .in0(multiplexer_8_out), .in1({mem_dout_2, mem_dout_1, mem_dout_0, mem_dout_3}), .out(mem_do),
    .sel(and_18_out));
  not not_7 (not_7_out, alu_res[1]);
  Multiplexer #(.width(32)) multiplexer_11 (
    .in0(mem_din), .in1({mem_din[23:0], mem_din[31:24]}), .out(multiplexer_11_out), .sel(and_19_out));
  and and_19 (and_19_out, alu_res[0], not_7_out);
  not not_8 (not_8_out, alu_res[0]);
  Multiplexer #(.width(32)) multiplexer_12 (
    .in0(multiplexer_11_out), .in1({mem_din[15:0], mem_din[31:16]}), .out(multiplexer_12_out),
    .sel(and_20_out));
  and and_20 (and_20_out, alu_res[1], not_8_out);
  Multiplexer #(.width(32)) multiplexer_13 (
    .in0(multiplexer_12_out), .in1({mem_din[7:0], mem_din[31:8]}), .out(mem_din_new), .sel(and_21_out));
  and and_21 (and_21_out, alu_res[1], alu_res[0]);

  // Other names for the same wires on the sheet: mem_din_1[7:0] = mem_din[15:8]; mem_din_2[7:0] = mem_din[23:16];
  //   mem_din_3[7:0] = mem_din[31:24]; mem_din_0[7:0] = mem_din[7:0]; addr[15:0] = alu_res[15:0]; align0 = alu_res[0];
  //   align1 = alu_res[1]; is_unsigned = funct3[2]
endmodule

module tmp (
);

  wire clk, control_en, mem_ren, mem_wen, rst, wb_en;
  wire [4:0] wb_addr;
  wire [7:0] mem_dout_0, mem_dout_1, mem_dout_2;
  wire [31:0] alu_res, control_pc, inst_addr, mem_addr, mem_din, mem_dout, wb_data;

  RAM ram_1 (.addr(alu_res[7:0]), .we(mem_wen), .oe(mem_ren), .clk(clk), .din(mem_din[7:0]), .dout(mem_dout_0));
  RAM ram_2 (.addr(alu_res[15:8]), .we(mem_wen), .oe(mem_ren), .clk(clk), .din(mem_din[15:8]), .dout(mem_dout_1));
  RAM ram_3 (.addr(alu_res[23:16]), .we(mem_wen), .oe(mem_ren), .clk(clk), .din(mem_din[23:16]), .dout(mem_dout_2));
  RAM ram_4 (.addr(alu_res[31:24]), .we(mem_wen), .oe(mem_ren), .clk(clk), .din(mem_din[31:24]), .dout(mem_dout_1));
  Multiplexer #(.width(32)) multiplexer_1 (.in0(inst_addr), .in1({32{1'b0}}), .out(inst_addr), .sel(rst));
  Multiplexer multiplexer_2 (.in0(mem_wen), .in1(1'b0), .out(mem_wen), .sel(rst));
  Multiplexer #(.width(5)) multiplexer_3 (.in0(wb_addr), .in1({5{1'b0}}), .out(wb_addr), .sel(rst));
  Multiplexer #(.width(32)) multiplexer_4 (.in0(wb_data), .in1({32{1'b0}}), .out(wb_data), .sel(rst));
  Multiplexer #(.width(32)) multiplexer_5 (.in0(mem_din), .in1({32{1'b0}}), .out(mem_din), .sel(rst));
  Multiplexer #(.width(32)) multiplexer_6 (.in0(mem_dout), .in1({32{1'b0}}), .out(mem_dout), .sel(rst));
  Multiplexer multiplexer_7 (.in0(control_en), .in1(1'b0), .out(control_en), .sel(rst));
  Multiplexer #(.width(32)) multiplexer_8 (.in0(mem_addr), .in1({32{1'b0}}), .out(mem_addr), .sel(rst));
  Multiplexer multiplexer_9 (.in0(wb_en), .in1(1'b0), .out(wb_en), .sel(rst));
  Multiplexer #(.width(32)) multiplexer_10 (.in0(control_pc), .in1({32{1'b0}}), .out(control_pc), .sel(rst));
endmodule
