// Logisim project proj_2_2_top.circ as structural Verilog: 8 circuits, main circuit TOP
module TOP (
  input  clk,
  input  rst,
  input  [31:0] inst,
  output [31:0] current_pc_if,
  output mem_wen_mem,
  output [31:0] mem_din_mem,
  output [31:0] mem_dout_mem,
  output [31:0] mem_addr_mem,
  output control_en_mem,
  output [31:0] control_pc_mem,
  output wb_en_wb,
  output [4:0] wb_addr_wb,
  output [31:0] wb_data_wb
);

  wire and_1_out, and_2_out, and_4_out, and_5_out, and_6_out, and_7_out, ASel_alu, ASel_id, BSel_alu,
       BSel_id, comparator_1_eq, comparator_2_eq, comparator_3_eq, comparator_4_eq, comparator_5_eq,
       comparator_6_eq, comparator_7_eq, comparator_8_eq, control_en_id, control_en_mem1, i_jalr_id,
       i_jalr_mem, instr_decoder_1_b_beq, instr_decoder_1_i_type, instr_decoder_1_j_jal,
       instr_decoder_1_r_type, instr_decoder_1_s_type, instr_decoder_1_u_auipc, instr_decoder_1_u_lui,
       load_id, load_mem, mem_ren_id, mem_ren_mem1, mem_wen_id, mem_wen_mem1, not_1_out, not_2_out,
       not_3_out, not_4_out, op_add_alu, op_add_id, op_and_alu, op_and_id, op_lt_alu, op_lt_id, op_ltu_alu,
       op_ltu_id, op_rs2_imm_alu, op_rs2_imm_id, op_sra_alu, op_sra_id, op_srl_alu, op_srl_id, or_1_out,
       or_2_out, or_3_out, or_4_out, or_5_out, or_6_out, or_7_out, or_8_out, or_9_out, register_10_q,
       register_21_q, register_26_q, register_28_q, register_33_q, register_42_q, register_43_q, wb_en_id,
       wb_en_wb1;
  wire [1:0] register_7_q, WBSel_alu, WBSel_id, WBSel_wb;
  wire [2:0] funct3_id, funct3_mem, register_40_q;
  wire [4:0] addrD_alu, addrD_id, addrD_mem, addrD_wb, rs1, rs2, wb_addr_wb1;
  wire [31:0] A_alu, A_id, A_id1, A_id_1, A_id_2, adder_1_out, alu_res_alu, alu_res_mem, alu_res_wb,
       and_3_out, B_alu, B_id, B_id1, B_id_1, B_id_2, B_mem, control_pc_mem1, current_pc_if1, imm_alu,
       imm_id, mem_dout_mem1, mem_dout_wb, multiplexer_1_out, multiplexer_14_out, multiplexer_15_out,
       register_1_q, register_9_q, register_11_q, register_14_q, register_16_q, register_18_q, register_22_q,
       wb_data_wb1;

  Adder #(.width(32)) adder_1 (.a(current_pc_if1), .b(32'h4), .out(adder_1_out));  // open: cin, cout
  Register #(.width(32)) register_1 (.D(inst), .clk(clk), .Q(register_1_q), .clr(or_2_out));  // open: en
  or or_1 (or_1_out, control_en_mem1, rst);
  Register #(.width(32)) register_2 (.D(multiplexer_1_out), .clk(clk), .Q(current_pc_if1), .clr(rst));  // open: en
  Multiplexer #(.width(32)) multiplexer_1 (
    .in0(adder_1_out), .in1(control_pc_mem1), .out(multiplexer_1_out), .sel(control_en_mem1));
  or or_2 (or_2_out, control_en_mem1, rst);
  Register #(.width(5)) register_3 (.D(addrD_id), .clk(clk), .Q(addrD_alu), .clr(or_1_out));  // open: en
  Register #(.width(5)) register_4 (.D(addrD_alu), .clk(clk), .Q(addrD_mem), .clr(rst));  // open: en
  Comparator #(.width(5)) comparator_1 (.a(addrD_mem), .b(rs1), .eq(comparator_1_eq));  // open: gt, lt
  not not_1 (not_1_out, load_mem);
  Register #(.width(5)) register_5 (.D(addrD_mem), .clk(clk), .Q(addrD_wb), .clr(rst));  // open: en
  Comparator #(.width(5)) comparator_2 (.a(addrD_alu), .b(rs1), .eq(comparator_2_eq));  // open: gt, lt
  and and_1 (and_1_out, comparator_1_eq, not_1_out);
  not not_2 (not_2_out, comparator_2_eq);
  instr_decoder instr_decoder_1 (
    .inst(register_1_q), .rd(addrD_id), .rs1(rs1), .rs2(rs2), .imm(imm_id), .funct3(funct3_id),
    .I_type(instr_decoder_1_i_type), .S_type(instr_decoder_1_s_type), .b_beq(instr_decoder_1_b_beq),
    .u_lui(instr_decoder_1_u_lui), .u_auipc(instr_decoder_1_u_auipc), .j_jal(instr_decoder_1_j_jal),
    .R_type(instr_decoder_1_r_type), .i_jalr(i_jalr_id), .load(load_id));  // open: opcode, funct7
  Register #(.width(32)) register_6 (.D(imm_id), .clk(clk), .Q(imm_alu), .clr(or_3_out));  // open: en
  and and_2 (and_2_out, not_2_out, and_1_out);
  assign and_3_out = alu_res_mem & 32'hfffffffe;  // AND_Gate and_3, 32 bits wide
  Multiplexer #(.width(32)) multiplexer_2 (.in0(A_id_2), .in1(alu_res_mem), .out(A_id1), .sel(and_2_out));
  Multiplexer #(.width(32)) multiplexer_3 (.in0(alu_res_mem), .in1(and_3_out), .out(control_pc_mem1), .sel(i_jalr_mem));
  or or_3 (or_3_out, control_en_mem1, rst);
  or or_4 (or_4_out, control_en_mem1, rst);
  Register #(.width(2)) register_7 (.D(WBSel_alu), .clk(clk), .Q(register_7_q), .clr(rst));  // open: en
  RegFile regfile_1 (
    .DataD(wb_data_wb1), .clk(clk), .RegWEn(wb_en_wb1), .AddrD(addrD_wb), .AddrA(rs1), .AddrB(rs2),
    .rst(rst), .DataA(A_id), .DataB(B_id));
  Register #(.width(2)) register_8 (.D(register_7_q), .clk(clk), .Q(WBSel_wb), .clr(rst));  // open: en
  Comparator #(.width(5)) comparator_3 (.a(addrD_mem), .b(rs2), .eq(comparator_3_eq));  // open: gt, lt
  not not_3 (not_3_out, load_mem);
  or or_5 (or_5_out, control_en_mem1, rst);
  Register #(.width(32)) register_9 (.D(adder_1_out), .clk(clk), .Q(register_9_q), .clr(or_6_out));  // open: en
  Comparator #(.width(5)) comparator_4 (.a(addrD_alu), .b(rs2), .eq(comparator_4_eq));  // open: gt, lt
  and and_4 (and_4_out, comparator_3_eq, not_3_out);
  Register #(.width(1)) register_10 (.D(load_id), .clk(clk), .Q(register_10_q), .clr(or_5_out));  // open: en
  Register #(.width(32)) register_11 (.D(register_9_q), .clk(clk), .Q(register_11_q), .clr(or_6_out));  // open: en
  Register #(.width(1)) register_12 (.D(ASel_id), .clk(clk), .Q(ASel_alu), .clr(or_4_out));  // open: en
  not not_4 (not_4_out, comparator_4_eq);
  Register #(.width(1)) register_13 (.D(register_10_q), .clk(clk), .Q(load_mem), .clr(rst));  // open: en
  Multiplexer #(.width(5)) multiplexer_4 (.in0({5{1'b0}}), .in1(addrD_wb), .out(wb_addr_wb1), .sel(wb_en_wb1));
  Register #(.width(32)) register_14 (.D(register_11_q), .clk(clk), .Q(register_14_q), .clr(rst));  // open: en
  Register #(.width(1)) register_15 (.D(op_add_id), .clk(clk), .Q(op_add_alu), .clr(or_4_out));  // open: en
  and and_5 (and_5_out, not_4_out, and_4_out);
  Register #(.width(32)) register_16 (.D(register_14_q), .clk(clk), .Q(register_16_q), .clr(rst));  // open: en
  Controller controller_1 (
    .inst(register_1_q), .DataA(A_id1), .DataB(B_id1), .funct3(funct3_id), .b_beq(instr_decoder_1_b_beq),
    .i_jalr(i_jalr_id), .j_jal(instr_decoder_1_j_jal), .I_type(instr_decoder_1_i_type),
    .u_auipc(instr_decoder_1_u_auipc), .R_type(instr_decoder_1_r_type), .load(load_id),
    .S_type(instr_decoder_1_s_type), .u_lui(instr_decoder_1_u_lui), .mem_ren(mem_ren_id),
    .mem_wen(mem_wen_id), .control_en(control_en_id), .wb_en(wb_en_id), .A_sel(ASel_id), .B_sel(BSel_id),
    .wb_src(WBSel_id), .op_sra(op_sra_id), .op_srl(op_srl_id), .op_lt(op_lt_id), .op_ltu(op_ltu_id),
    .op_add(op_add_id), .op_and(op_and_id), .op_rs2_imm(op_rs2_imm_id));
  Multiplexer #(.width(32)) multiplexer_5 (.in0(B_id_2), .in1(alu_res_mem), .out(B_id1), .sel(and_5_out));
  Register #(.width(2)) register_17 (.D(WBSel_id), .clk(clk), .Q(WBSel_alu), .clr(or_4_out));  // open: en
  Comparator #(.width(5)) comparator_5 (.a(addrD_alu), .b(rs1), .eq(comparator_5_eq));  // open: gt, lt
  Multiplexer #(.width(32)) multiplexer_6 (.in0(current_pc_if1), .in1({32{1'b0}}), .out(current_pc_if), .sel(rst));
  Multiplexer multiplexer_7 (.in0(mem_wen_mem1), .in1(1'b0), .out(mem_wen_mem), .sel(rst));
  Multiplexer #(.width(5)) multiplexer_8 (.in0(wb_addr_wb1), .in1({5{1'b0}}), .out(wb_addr_wb), .sel(rst));
  Multiplexer #(.width(32)) multiplexer_9 (.in0(A_id), .in1(alu_res_alu), .out(A_id_1), .sel(comparator_5_eq));
  or or_6 (or_6_out, control_en_mem1, rst);
  Register #(.width(32)) register_18 (.D(current_pc_if1), .clk(clk), .Q(register_18_q), .clr(or_6_out));  // open: en
  Register #(.width(1)) register_19 (.D(op_lt_id), .clk(clk), .Q(op_lt_alu), .clr(or_4_out));  // open: en
  Multiplexer #(.select(2), .width(32)) multiplexer_10 (
    .in0(alu_res_wb), .in1(mem_dout_wb), .in2(register_16_q), .out(wb_data_wb1), .sel(WBSel_wb));  // open: in3
  Register #(.width(1)) register_20 (.D(op_srl_id), .clk(clk), .Q(op_srl_alu), .clr(or_4_out));  // open: en
  Register #(.width(1)) register_21 (.D(i_jalr_id), .clk(clk), .Q(register_21_q), .clr(or_7_out));  // open: en
  Register #(.width(32)) register_22 (.D(register_18_q), .clk(clk), .Q(register_22_q), .clr(or_6_out));  // open: en
  Multiplexer #(.width(32)) multiplexer_11 (.in0(wb_data_wb1), .in1({32{1'b0}}), .out(wb_data_wb), .sel(rst));
  Register #(.width(1)) register_23 (.D(register_21_q), .clk(clk), .Q(i_jalr_mem), .clr(rst));  // open: en
  or or_7 (or_7_out, control_en_mem1, rst);
  ALU alu_1 (
    .rsa(multiplexer_14_out), .rsb_imm(multiplexer_15_out), .op_add(op_add_alu), .op_lt(op_lt_alu),
    .op_ltu(op_ltu_alu), .op_and(op_and_alu), .op_srl(op_srl_alu), .op_sra(op_sra_alu),
    .op_rs2_imm(op_rs2_imm_alu), .dout(alu_res_alu));  // open: op_eq, op_equ
  Comparator #(.width(5)) comparator_6 (.a(addrD_alu), .b(rs2), .eq(comparator_6_eq));  // open: gt, lt
  Multiplexer #(.width(32)) multiplexer_12 (.in0(B_mem), .in1({32{1'b0}}), .out(mem_din_mem), .sel(rst));
  Multiplexer #(.width(32)) multiplexer_13 (.in0(mem_dout_mem1), .in1({32{1'b0}}), .out(mem_dout_mem), .sel(rst));
  Multiplexer #(.width(32)) multiplexer_14 (.in0(A_alu), .in1(register_22_q), .out(multiplexer_14_out), .sel(ASel_alu));
  Multiplexer #(.width(32)) multiplexer_15 (.in0(B_alu), .in1(imm_alu), .out(multiplexer_15_out), .sel(BSel_alu));
  Register #(.width(1)) register_24 (.D(BSel_id), .clk(clk), .Q(BSel_alu), .clr(or_4_out));  // open: en
  Multiplexer #(.width(32)) multiplexer_16 (.in0(B_id), .in1(alu_res_alu), .out(B_id_1), .sel(comparator_6_eq));
  or or_8 (or_8_out, control_en_mem1, rst);
  Register #(.width(1)) register_25 (.D(op_ltu_id), .clk(clk), .Q(op_ltu_alu), .clr(or_4_out));  // open: en
  Multiplexer multiplexer_17 (.in0(control_en_mem1), .in1(1'b0), .out(control_en_mem), .sel(rst));
  Register #(.width(1)) register_26 (.D(wb_en_id), .clk(clk), .Q(register_26_q), .clr(or_8_out));  // open: en
  Register #(.width(32)) register_27 (.D(alu_res_alu), .clk(clk), .Q(alu_res_mem), .clr(rst));  // open: en
  Multiplexer #(.width(32)) multiplexer_18 (.in0(alu_res_mem), .in1({32{1'b0}}), .out(mem_addr_mem), .sel(rst));
  Memory memory_1 (
    .alu_res(alu_res_mem), .mem_wen(mem_wen_mem1), .mem_ren(mem_ren_mem1), .clk(clk), .mem_din(B_mem),
    .funct3(funct3_mem), .mem_dout(mem_dout_mem1));
  Register #(.width(1)) register_28 (.D(register_26_q), .clk(clk), .Q(register_28_q), .clr(rst));  // open: en
  Register #(.width(1)) register_29 (.D(op_and_id), .clk(clk), .Q(op_and_alu), .clr(or_4_out));  // open: en
  Register #(.width(1)) register_30 (.D(op_sra_id), .clk(clk), .Q(op_sra_alu), .clr(or_4_out));  // open: en
  Register #(.width(1)) register_31 (.D(register_28_q), .clk(clk), .Q(wb_en_wb1), .clr(rst));  // open: en
  Comparator #(.width(5)) comparator_7 (.a(addrD_mem), .b(rs1), .eq(comparator_7_eq));  // open: gt, lt
  Multiplexer #(.width(32)) multiplexer_19 (.in0(A_id_1), .in1(mem_dout_mem1), .out(A_id_2), .sel(and_6_out));
  and and_6 (and_6_out, comparator_7_eq, load_mem);
  Multiplexer multiplexer_20 (.in0(wb_en_wb1), .in1(1'b0), .out(wb_en_wb), .sel(rst));
  Register #(.width(32)) register_32 (.D(A_id1), .clk(clk), .Q(A_alu), .clr(or_4_out));  // open: en
  Multiplexer #(.width(32)) multiplexer_21 (.in0(control_pc_mem1), .in1({32{1'b0}}), .out(control_pc_mem), .sel(rst));
  Register #(.width(1)) register_33 (.D(mem_ren_id), .clk(clk), .Q(register_33_q), .clr(or_8_out));  // open: en
  Register #(.width(1)) register_34 (.D(op_rs2_imm_id), .clk(clk), .Q(op_rs2_imm_alu), .clr(or_4_out));  // open: en
  Comparator #(.width(5)) comparator_8 (.a(addrD_mem), .b(rs2), .eq(comparator_8_eq));  // open: gt, lt
  Register #(.width(32)) register_35 (.D(mem_dout_mem1), .clk(clk), .Q(mem_dout_wb), .clr(rst));  // open: en
  Register #(.width(32)) register_36 (.D(alu_res_mem), .clk(clk), .Q(alu_res_wb), .clr(rst));  // open: en
  Register #(.width(1)) register_37 (.D(register_33_q), .clk(clk), .Q(mem_ren_mem1), .clr(rst));  // open: en
  Register #(.width(32)) register_38 (.D(B_id1), .clk(clk), .Q(B_alu), .clr(or_4_out));  // open: en
  Multiplexer #(.width(32)) multiplexer_22 (.in0(B_id_1), .in1(mem_dout_mem1), .out(B_id_2), .sel(and_7_out));
  and and_7 (and_7_out, comparator_8_eq, load_mem);
  Register #(.width(32)) register_39 (.D(imm_id), .clk(clk), .Q(imm_alu), .clr(or_4_out));  // open: en
  Register #(.width(3)) register_40 (.D(funct3_id), .clk(clk), .Q(register_40_q), .clr(or_9_out));  // open: en
  or or_9 (or_9_out, control_en_mem1, rst);
  Register #(.width(3)) register_41 (.D(register_40_q), .clk(clk), .Q(funct3_mem), .clr(rst));  // open: en
  Register #(.width(1)) register_42 (.D(mem_wen_id), .clk(clk), .Q(register_42_q), .clr(or_8_out));  // open: en
  Register #(.width(1)) register_43 (.D(control_en_id), .clk(clk), .Q(register_43_q), .clr(or_8_out));  // open: en
  Register #(.width(1)) register_44 (.D(register_42_q), .clk(clk), .Q(mem_wen_mem1), .clr(rst));  // open: en
  Register #(.width(32)) register_45 (.D(B_alu), .clk(clk), .Q(B_mem), .clr(rst));  // open: en
  Register #(.width(1)) register_46 (.D(register_43_q), .clk(clk), .Q(control_en_mem1), .clr(rst));  // open: en

  // Other names for the same wires on the sheet: mem_addr_mem1[31:0] = alu_res_mem; mem_din_mem1[31:0] = B_mem

  // Notes on the sheet:
  //   DON'T TOUCH!
  //   IF stage output
  //   MEM stage output
  //   WB stage output
endmodule

module testbench (
  input  rst,
  output [7:0] out_2,
  output [31:0] current_pc_if,
  output mem_wen_mem,
  output halt,
  output [31:0] mem_din_mem,
  output [31:0] mem_dout_mem,
  output [31:0] mem_addr_mem,
  output control_en_mem,
  output [31:0] control_pc_mem,
  output wb_en_wb,
  output [4:0] wb_addr_wb,
  output [31:0] wb_data_wb
);

  wire and_1_out, carry, clk, mem_wen_men, not_1_out, not_2_out, por_1_out, rst_t;
  wire [31:0] inst;

  not not_1 (not_1_out, inst[2]);
  not not_2 (not_2_out, inst[3]);
  POR por_1 (.out(por_1_out));
  TOP top_1 (
    .clk(clk), .rst(rst_t), .inst(inst), .current_pc_if(current_pc_if), .mem_wen_mem(mem_wen_men),
    .mem_din_mem(mem_din_mem), .mem_dout_mem(mem_dout_mem), .mem_addr_mem(mem_addr_mem),
    .control_en_mem(control_en_mem), .control_pc_mem(control_pc_mem), .wb_en_wb(wb_en_wb),
    .wb_addr_wb(wb_addr_wb), .wb_data_wb(wb_data_wb));
  Clock clock_1 (.out(clk));
  or or_1 (rst_t, rst, por_1_out);
  and and_1 (and_1_out, inst[0], inst[1], not_1_out, not_2_out, inst[4], inst[5], inst[6]);
  or or_2 (halt, and_1_out, carry);
  Counter counter_1 (.clr(rst_t), .up(1'b1), .count(1'b1), .clk(clk), .carry(carry), .Q(out_2));  // open: load, D
  // ROM #(.line("quad"), .misaligned("true")) rom_1: pin names not known; wires that end beside it: current_pc_if[7:0], inst[7:0], inst[15:8], inst[23:16], inst[31:24]
  // Probe on inst

  // Notes on the sheet:
  //   DON'T TOUCH!
  //   IF stage output
  //   MEM stage output
  //   WB stage output
  //   test
endmodule

module ALU (
  input  [31:0] rsa,
  input  [31:0] rsb_imm,
  input  op_add,
  input  op_eq,
  input  op_lt,
  input  op_equ,
  input  op_ltu,
  input  op_and,
  input  op_srl,
  input  op_sra,
  input  op_rs2_imm,
  output [31:0] dout
);

  wire comparator_1_eq, comparator_1_gt, comparator_1_lt, comparator_2_eq, comparator_2_lt,
       multiplexer_1_out, multiplexer_2_out, multiplexer_3_out, multiplexer_4_out, or_1_out;
  wire [31:0] adder_1_out, and_1_out, bit_extender_1_out, multiplexer_5_out, multiplexer_6_out,
       multiplexer_7_out, multiplexer_8_out, shifter_1_out, shifter_2_out;

  // Probe on op_add
  Adder #(.width(32)) adder_1 (.a(rsa), .b(rsb_imm), .out(adder_1_out));  // open: cin, cout
  assign and_1_out = rsa & rsb_imm;  // AND_Gate and_1, 32 bits wide
  Shifter #(.shift("lr"), .width(32)) shifter_1 (.in(rsa), .\dist (rsb_imm[4:0]), .out(shifter_1_out));
  Shifter #(.shift("ar"), .width(32)) shifter_2 (.in(rsa), .\dist (rsb_imm[4:0]), .out(shifter_2_out));
  Comparator #(.width(32)) comparator_1 (
    .a(rsa), .b(rsb_imm), .gt(comparator_1_gt), .eq(comparator_1_eq), .lt(comparator_1_lt));
  Comparator #(.mode("unsigned"), .width(32)) comparator_2 (
    .a(rsa), .b(rsb_imm), .eq(comparator_2_eq), .lt(comparator_2_lt));  // open: gt
  Multiplexer multiplexer_1 (.in0(comparator_1_gt), .in1(comparator_1_eq), .out(multiplexer_1_out), .sel(op_eq));
  Multiplexer multiplexer_2 (.in0(multiplexer_1_out), .in1(comparator_1_lt), .out(multiplexer_2_out), .sel(op_lt));
  Multiplexer multiplexer_3 (.in0(multiplexer_2_out), .in1(comparator_2_eq), .out(multiplexer_3_out), .sel(op_equ));
  assign bit_extender_1_out = {{31{1'b0}}, multiplexer_4_out};  // Bit_Extender bit_extender_1
  Multiplexer multiplexer_4 (.in0(multiplexer_3_out), .in1(comparator_2_lt), .out(multiplexer_4_out), .sel(op_ltu));
  or or_1 (or_1_out, op_eq, op_ltu, op_lt, op_equ);
  Multiplexer #(.width(32)) multiplexer_5 (.in0(adder_1_out), .in1(and_1_out), .out(multiplexer_5_out), .sel(op_and));
  Multiplexer #(.width(32)) multiplexer_6 (
    .in0(multiplexer_5_out), .in1(shifter_1_out), .out(multiplexer_6_out), .sel(op_srl));
  Multiplexer #(.width(32)) multiplexer_7 (
    .in0(multiplexer_6_out), .in1(shifter_2_out), .out(multiplexer_7_out), .sel(op_sra));
  Multiplexer #(.width(32)) multiplexer_8 (
    .in0(multiplexer_7_out), .in1(bit_extender_1_out), .out(multiplexer_8_out), .sel(or_1_out));
  Multiplexer #(.width(32)) multiplexer_9 (.in0(multiplexer_8_out), .in1(rsb_imm), .out(dout), .sel(op_rs2_imm));

  // Notes on the sheet:
  //   unsigned
endmodule

module imm_gen (
  input  [31:0] inst,
  output [31:0] I_imm,
  output [31:0] S_imm,
  output [31:0] B_imm,
  output [31:0] U_imm,
  output [31:0] J_imm
);

  // NoConnect on inst[6:0]
  assign {I_imm[31], B_imm[31:12]} = {{20{inst[31]}}, inst[31]};  // Bit_Extender bit_extender_1
  // NoConnect on I_imm[31]
  // NoConnect on {I_imm[31], B_imm[31:13]}
  // NoConnect on {I_imm[31], B_imm[31:24]}

  assign B_imm[11:0] = {inst[7], inst[30:25], inst[11:8], 1'b0};
  assign I_imm[30:0] = {B_imm[31:12], inst[30:20]};
  assign J_imm = {B_imm[23:12], inst[19:12], inst[20], inst[30:21], 1'b0};
  assign S_imm = {I_imm[31], B_imm[31:12], inst[30:25], inst[11:7]};
  assign U_imm = {B_imm[12], inst[30:12], {12{1'b0}}};

  // Notes on the sheet:
  //   I-imm
  //   S-imm
  //   B-imm
  //   U-imm
  //   J-imm
endmodule

module instr_decoder (
  input  [31:0] inst,
  output [6:0] opcode,
  output [4:0] rd,
  output [4:0] rs1,
  output [4:0] rs2,
  output [31:0] imm,
  output [2:0] funct3,
  output [6:0] funct7,
  output I_type,
  output S_type,
  output b_beq,
  output u_lui,
  output u_auipc,
  output j_jal,
  output R_type,
  output i_jalr,
  output load
);

  wire or_1_out, or_2_out, or_3_out;
  wire [31:0] imm_gen_1_b_imm, imm_gen_1_i_imm, imm_gen_1_j_imm, imm_gen_1_s_imm, imm_gen_1_u_imm,
       multiplexer_1_out, multiplexer_2_out, multiplexer_3_out, multiplexer_4_out;

  // Probe on inst
  Comparator #(.width(7)) comparator_1 (.a(inst[6:0]), .b(7'b0010011), .eq(I_type));  // open: gt, lt
  Comparator #(.width(7)) comparator_2 (.a(inst[6:0]), .b(7'b0100011), .eq(S_type));  // open: gt, lt
  Comparator #(.width(7)) comparator_3 (.a(inst[6:0]), .b(7'b1100011), .eq(b_beq));  // open: gt, lt
  Comparator #(.width(7)) comparator_4 (.a(inst[6:0]), .b(7'b0110111), .eq(u_lui));  // open: gt, lt
  Comparator #(.width(7)) comparator_5 (.a(inst[6:0]), .b(7'b0010111), .eq(u_auipc));  // open: gt, lt
  Comparator #(.width(7)) comparator_6 (.a(inst[6:0]), .b(7'b1101111), .eq(j_jal));  // open: gt, lt
  Comparator #(.width(7)) comparator_7 (.a(inst[6:0]), .b(7'b0110011), .eq(R_type));  // open: gt, lt
  Comparator #(.width(7)) comparator_8 (.a(inst[6:0]), .b(7'b1100111), .eq(i_jalr));  // open: gt, lt
  Comparator #(.width(7)) comparator_9 (.a(inst[6:0]), .b(7'b0000011), .eq(load));  // open: gt, lt
  imm_gen imm_gen_1 (
    .inst(inst), .I_imm(imm_gen_1_i_imm), .S_imm(imm_gen_1_s_imm), .B_imm(imm_gen_1_b_imm),
    .U_imm(imm_gen_1_u_imm), .J_imm(imm_gen_1_j_imm));
  or or_1 (or_1_out, u_lui, u_auipc);
  or or_2 (or_2_out, i_jalr, load);
  Multiplexer #(.width(32)) multiplexer_1 (
    .in0({32{1'b0}}), .in1(imm_gen_1_i_imm), .out(multiplexer_1_out), .sel(or_3_out));
  or or_3 (or_3_out, I_type, or_2_out);
  Multiplexer #(.width(32)) multiplexer_2 (
    .in0(multiplexer_1_out), .in1(imm_gen_1_s_imm), .out(multiplexer_2_out), .sel(S_type));
  Multiplexer #(.width(32)) multiplexer_3 (
    .in0(multiplexer_2_out), .in1(imm_gen_1_b_imm), .out(multiplexer_3_out), .sel(b_beq));
  Multiplexer #(.width(32)) multiplexer_4 (
    .in0(multiplexer_3_out), .in1(imm_gen_1_u_imm), .out(multiplexer_4_out), .sel(or_1_out));
  Multiplexer #(.width(32)) multiplexer_5 (.in0(multiplexer_4_out), .in1(imm_gen_1_j_imm), .out(imm), .sel(j_jal));

  assign funct3 = inst[14:12];
  assign funct7 = inst[31:25];
  assign opcode = inst[6:0];
  assign rd = inst[11:7];
  assign rs1 = inst[19:15];
  assign rs2 = inst[24:20];
endmodule

module Controller (
  input  [31:0] inst,
  input  [31:0] DataA,
  input  [31:0] DataB,
  input  [2:0] funct3,
  input  b_beq,
  input  i_jalr,
  input  j_jal,
  input  I_type,
  input  u_auipc,
  input  R_type,
  input  load,
  input  S_type,
  input  u_lui,
  output mem_ren,
  output mem_wen,
  output control_en,
  output wb_en,
  output A_sel,
  output B_sel,
  output [1:0] wb_src,
  output op_sra,
  output op_srl,
  output op_lt,
  output op_ltu,
  output op_add,
  output op_and,
  output op_rs2_imm
);

  wire and_4_out, comparator_1_eq, comparator_2_eq, comparator_3_eq, comparator_4_eq, comparator_5_eq,
       comparator_7_eq, comparator_8_eq, comparator_9_eq, comparator_10_eq, comparator_11_eq,
       comparator_12_eq, comparator_13_eq, i_addi, i_lh, i_lw, r_add, s_sh, s_sw;
  wire [1:0] or_7_out;
  wire [6:0] funct7;

  Comparator #(.width(3)) comparator_1 (.a(funct3), .b(3'b011), .eq(comparator_1_eq));  // open: gt, lt
  and and_1 (op_ltu, comparator_1_eq, I_type);
  Comparator #(.width(3)) comparator_2 (.a(funct3), .b(3'b001), .eq(comparator_2_eq));  // open: gt, lt
  Comparator #(.width(3)) comparator_3 (.a(funct3), .b(3'b010), .eq(comparator_3_eq));  // open: gt, lt
  Comparator #(.width(32)) comparator_4 (.a(DataB), .b(DataA), .eq(comparator_4_eq));  // open: gt, lt
  and and_2 (i_lh, comparator_2_eq, load);
  and and_3 (i_lw, comparator_3_eq, load);
  Comparator #(.width(3)) comparator_5 (.a(funct3), .b(3'b000), .eq(comparator_5_eq));  // open: gt, lt
  Comparator #(.width(7)) comparator_6 (.a(funct7));  // open: b, gt, eq, lt
  Comparator #(.width(3)) comparator_7 (.a(funct3), .b(3'b010), .eq(comparator_7_eq));  // open: gt, lt
  or or_1 (op_add, r_add, i_addi, i_lw, i_lh, i_jalr, u_auipc, s_sw, s_sh, j_jal);
  and and_4 (and_4_out, comparator_4_eq, b_beq);
  and and_5 (r_add, comparator_5_eq, R_type);
  and and_6 (s_sw, comparator_7_eq, S_type);
  or or_2 (control_en, and_4_out, i_jalr, j_jal);
  or or_3 (wb_en, i_jalr, j_jal, I_type, u_auipc, u_lui, R_type, load);
  Comparator #(.width(3)) comparator_8 (.a(funct3), .b(3'b000), .eq(comparator_8_eq));  // open: gt, lt
  and and_7 (i_addi, comparator_8_eq, I_type);
  Comparator #(.width(3)) comparator_9 (.a(funct3), .b(3'b101), .eq(comparator_9_eq));  // open: gt, lt
  Comparator #(.width(3)) comparator_10 (.a(funct3), .b(3'b001), .eq(comparator_10_eq));  // open: gt, lt
  or or_4 (A_sel, u_auipc, u_lui, b_beq, j_jal);
  and and_8 (op_sra, comparator_9_eq, R_type);
  and and_9 (s_sh, comparator_10_eq, S_type);
  Comparator #(.width(3)) comparator_11 (.a(funct3), .b(3'b101), .eq(comparator_11_eq));  // open: gt, lt
  and and_10 (op_srl, comparator_11_eq, I_type);
  // Probe on B_sel
  or or_5 (B_sel, A_sel, op_ltu, i_jalr, i_addi, op_srl, op_and, i_lh, i_lw, s_sw, s_sh);
  Comparator #(.width(3)) comparator_12 (.a(funct3), .b(3'b010), .eq(comparator_12_eq));  // open: gt, lt
  and and_11 (op_lt, comparator_12_eq, R_type);
  Comparator #(.width(3)) comparator_13 (.a(funct3), .b(3'b111), .eq(comparator_13_eq));  // open: gt, lt
  or or_6 (or_7_out[1], i_jalr, j_jal);
  and and_12 (op_and, comparator_13_eq, I_type);
  Multiplexer #(.select(2), .width(2)) multiplexer_1 (
    .in0(2'b00), .in1(2'b01), .in2(2'b10), .out(wb_src), .sel(or_7_out));  // open: in3
  or or_7 (or_7_out[0], i_lh, i_lw);
  // Probe on wb_src

  assign mem_ren = load;
  assign mem_wen = S_type;
  assign op_rs2_imm = u_lui;

  // Other names for the same wires on the sheet: i_andi = op_and; i_sltiu = op_ltu; i_srli = op_srl; r_slt = op_lt;
  //   r_sra = op_sra

  // Notes on the sheet:
  //   PC_sel
  //   RegWen
endmodule

module Memory (
  input  [31:0] alu_res,
  input  mem_wen,
  input  mem_ren,
  input  clk,
  input  [31:0] mem_din,
  input  [2:0] funct3,
  output [31:0] mem_dout
);

  wire and_1_out, and_2_out, and_3_out, and_7_out, and_8_out, and_9_out, and_10_out, and_14_out, and_16_out,
       and_18_out, and_19_out, and_20_out, and_21_out, is_b, is_h, is_w, mem_wen_0, mem_wen_1, mem_wen_2,
       mem_wen_3, nor_1_out, nor_2_out, nor_3_out, not_1_out, not_2_out, not_3_out, not_4_out, not_5_out,
       not_6_out, not_7_out, not_8_out, or_1_out, or_2_out, or_3_out, or_4_out, or_5_out, or_6_out, or_7_out,
       or_8_out, or_9_out;
  wire [7:0] mem_dout_0, mem_dout_1, mem_dout_2, mem_dout_3;
  wire [15:0] addr_align, addr_alignoffset, multiplexer_1_out, multiplexer_2_out, multiplexer_3_out,
       multiplexer_4_out, multiplexer_5_out;
  wire [31:0] bit_extender_1_out, mem_din_new, mem_do, multiplexer_6_out, multiplexer_7_out,
       multiplexer_8_out, multiplexer_11_out, multiplexer_12_out;

  Multiplexer #(.width(16)) multiplexer_1 (
    .in0(addr_alignoffset), .in1(alu_res[15:0]), .out(multiplexer_1_out), .sel(nor_1_out));
  nor nor_1 (nor_1_out, alu_res[0], alu_res[1]);
  Multiplexer #(.width(16)) multiplexer_2 (
    .in0(alu_res[15:0]), .in1(addr_align), .out(multiplexer_2_out), .sel(alu_res[0]));
  Multiplexer #(.width(16)) multiplexer_3 (
    .in0(alu_res[15:0]), .in1(addr_align), .out(multiplexer_3_out), .sel(or_1_out));
  or or_1 (or_1_out, alu_res[0], alu_res[1]);
  and and_1 (and_1_out, alu_res[0], alu_res[1]);
  Multiplexer #(.width(16)) multiplexer_4 (
    .in0(multiplexer_2_out), .in1(addr_alignoffset), .out(multiplexer_4_out), .sel(alu_res[1]));
  Multiplexer #(.width(16)) multiplexer_5 (
    .in0(multiplexer_3_out), .in1(addr_alignoffset), .out(multiplexer_5_out), .sel(and_1_out));
  nor nor_2 (nor_2_out, alu_res[0], alu_res[1]);
  not not_1 (not_1_out, alu_res[1]);
  RAM #(.addrWidth(16), .asyncread("true"), .clearpin("true"), .trigger("falling")) ram_1 (
    .addr(multiplexer_1_out), .we(mem_wen_0), .oe(mem_ren), .clk(clk), .din(mem_din_new[7:0]),
    .dout(mem_dout_0));  // open: clr
  RAM #(.addrWidth(16), .asyncread("true"), .clearpin("true"), .trigger("falling")) ram_2 (
    .addr(multiplexer_4_out), .we(mem_wen_1), .oe(mem_ren), .clk(clk), .din(mem_din_new[15:8]),
    .dout(mem_dout_1));  // open: clr
  RAM #(.addrWidth(16), .asyncread("true"), .clearpin("true"), .trigger("falling")) ram_3 (
    .addr(multiplexer_5_out), .we(mem_wen_2), .oe(mem_ren), .clk(clk), .din(mem_din_new[23:16]),
    .dout(mem_dout_2));  // open: clr
  RAM #(.addrWidth(16), .asyncread("true"), .clearpin("true"), .trigger("falling")) ram_4 (
    .addr(addr_align), .we(mem_wen_3), .oe(mem_ren), .clk(clk), .din(mem_din_new[31:24]), .dout(mem_dout_3));  // open: clr
  or or_2 (or_2_out, nor_2_out, and_2_out);
  and and_2 (and_2_out, alu_res[0], alu_res[1]);
  nor nor_3 (nor_3_out, alu_res[0], alu_res[1]);
  and and_3 (and_3_out, alu_res[0], not_1_out);
  or or_3 (or_3_out, nor_3_out, and_3_out);
  or or_4 (or_4_out, or_2_out, is_w);
  and and_4 (mem_wen_0, mem_wen, or_4_out);
  or or_5 (or_5_out, or_3_out, is_w);
  and and_5 (mem_wen_1, mem_wen, or_5_out);
  assign addr_align = alu_res[15:0] & 16'hfffc;  // AND_Gate and_6, 16 bits wide
  not not_2 (not_2_out, alu_res[0]);
  and and_7 (and_7_out, alu_res[1], not_2_out);
  not not_3 (not_3_out, alu_res[1]);
  not not_4 (not_4_out, alu_res[0]);
  and and_8 (and_8_out, alu_res[0], not_3_out);
  and and_9 (and_9_out, alu_res[1], not_4_out);
  not not_5 (not_5_out, alu_res[1]);
  or or_6 (or_6_out, and_7_out, and_8_out);
  and and_10 (and_10_out, alu_res[0], alu_res[1]);
  and and_11 (is_b, ~funct3[0], ~funct3[1]);  // AND_Gate
  and and_12 (is_h, funct3[0], ~funct3[1]);  // AND_Gate
  and and_13 (is_w, ~funct3[0], funct3[1]);  // AND_Gate
  and and_14 (and_14_out, alu_res[0], not_5_out);
  or or_7 (or_7_out, and_9_out, and_10_out);
  Multiplexer #(.width(32)) multiplexer_6 (
    .in0({mem_dout_3, mem_dout_2, mem_dout_1, mem_dout_0}),
    .in1({mem_dout_0, mem_dout_3, mem_dout_2, mem_dout_1}), .out(multiplexer_6_out), .sel(and_14_out));
  or or_8 (or_8_out, or_6_out, is_w);
  and and_15 (mem_wen_2, mem_wen, or_8_out);
  or or_9 (or_9_out, or_7_out, is_w);
  and and_16 (and_16_out, alu_res[1], not_6_out);
  not not_6 (not_6_out, alu_res[0]);
  and and_17 (mem_wen_3, mem_wen, or_9_out);
  Adder #(.width(16)) adder_1 (.a(addr_align), .b(16'h4), .out(addr_alignoffset));  // open: cin, cout
  Multiplexer #(.width(32)) multiplexer_7 (.in0({32{1'b0}}), .in1(mem_do), .out(multiplexer_7_out), .sel(mem_ren));
  Multiplexer #(.width(32)) multiplexer_8 (
    .in0(multiplexer_6_out), .in1({mem_dout_1, mem_dout_0, mem_dout_3, mem_dout_2}), .out(multiplexer_8_out),
    .sel(and_16_out));
  assign bit_extender_1_out = {{16{multiplexer_7_out[15]}}, multiplexer_7_out[15:0]};  // Bit_Extender bit_extender_1
  Multiplexer #(.width(32)) multiplexer_9 (
    .in0(multiplexer_7_out), .in1(bit_extender_1_out), .out(mem_dout), .sel(is_h));
  and and_18 (and_18_out, alu_res[1], alu_res[0]);
  Multiplexer #(.width(32)) multiplexer_10 (
    .in0(multiplexer_8_out), .in1({mem_dout_2, mem_dout_1, mem_dout_0, mem_dout_3}), .out(mem_do),
    .sel(and_18_out));
  not not_7 (not_7_out, alu_res[1]);
  Multiplexer #(.width(32)) multiplexer_11 (
    .in0(mem_din), .in1({mem_din[23:0], mem_din[31:24]}), .out(multiplexer_11_out), .sel(and_19_out));
  and and_19 (and_19_out, alu_res[0], not_7_out);
  not not_8 (not_8_out, alu_res[0]);
  Multiplexer #(.width(32)) multiplexer_12 (
    .in0(multiplexer_11_out), .in1({mem_din[15:0], mem_din[31:16]}), .out(multiplexer_12_out),
    .sel(and_20_out));
  and and_20 (and_20_out, alu_res[1], not_8_out);
  Multiplexer #(.width(32)) multiplexer_13 (
    .in0(multiplexer_12_out), .in1({mem_din[7:0], mem_din[31:8]}), .out(mem_din_new), .sel(and_21_out));
  and and_21 (and_21_out, alu_res[1], alu_res[0]);

  // Other names for the same wires on the sheet: mem_din_1[7:0] = mem_din[15:8]; mem_din_2[7:0] = mem_din[23:16];
  //   mem_din_3[7:0] = mem_din[31:24]; mem_din_0[7:0] = mem_din[7:0]; addr[15:0] = alu_res[15:0]; align0 = alu_res[0];
  //   align1 = alu_res[1]; is_unsigned = funct3[2]
endmodule

module RegFile (
  input  [31:0] DataD,
  input  clk,
  input  RegWEn,
  input  [4:0] AddrD,
  input  [4:0] AddrA,
  input  [4:0] AddrB,
  input  rst,
  output [31:0] DataA,
  output [31:0] DataB
);

  wire AddrD_x0, AddrD_x1, AddrD_x2, AddrD_x3, AddrD_x4, AddrD_x5, AddrD_x6, AddrD_x7, AddrD_x8, AddrD_x9,
       AddrD_x10, AddrD_x11, AddrD_x12, AddrD_x13, AddrD_x14, AddrD_x15, AddrD_x16, AddrD_x17, AddrD_x18,
       AddrD_x19, AddrD_x20, AddrD_x21, AddrD_x22, AddrD_x23, AddrD_x24, AddrD_x25, AddrD_x26, AddrD_x27,
       AddrD_x28, AddrD_x29, AddrD_x30, AddrD_x31;
  wire [31:0] Data_x0, Data_x1, Data_x2, Data_x3, Data_x4, Data_x5, Data_x6, Data_x7, Data_x8, Data_x9,
       Data_x10, Data_x11, Data_x12, Data_x13, Data_x14, Data_x15, Data_x16, Data_x17, Data_x18, Data_x19,
       Data_x20, Data_x21, Data_x22, Data_x23, Data_x24, Data_x25, Data_x26, Data_x27, Data_x28, Data_x29,
       Data_x30, Data_x31;

  Demultiplexer #(.select(5)) demultiplexer_1 (
    .out0(AddrD_x0), .out1(AddrD_x1), .out2(AddrD_x2), .out3(AddrD_x3), .out4(AddrD_x4), .out5(AddrD_x5),
    .out6(AddrD_x6), .out7(AddrD_x7), .out8(AddrD_x8), .out9(AddrD_x9), .out10(AddrD_x10), .out11(AddrD_x11),
    .out12(AddrD_x12), .out13(AddrD_x13), .out14(AddrD_x14), .out15(AddrD_x15), .out16(AddrD_x16),
    .out17(AddrD_x17), .out18(AddrD_x18), .out19(AddrD_x19), .out20(AddrD_x20), .out21(AddrD_x21),
    .out22(AddrD_x22), .out23(AddrD_x23), .out24(AddrD_x24), .out25(AddrD_x25), .out26(AddrD_x26),
    .out27(AddrD_x27), .out28(AddrD_x28), .out29(AddrD_x29), .out30(AddrD_x30), .out31(AddrD_x31),
    .in(RegWEn), .sel(AddrD));
  Register #(.trigger("falling"), .width(32)) x0 (.D(DataD), .en(AddrD_x0), .clk(clk), .Q(Data_x0), .clr(rst));
  Register #(.trigger("falling"), .width(32)) x1 (.D(DataD), .en(AddrD_x1), .clk(clk), .Q(Data_x1), .clr(rst));
  Register #(.trigger("falling"), .width(32)) x2 (.D(DataD), .en(AddrD_x2), .clk(clk), .Q(Data_x2), .clr(rst));
  Register #(.trigger("falling"), .width(32)) x3 (.D(DataD), .en(AddrD_x3), .clk(clk), .Q(Data_x3), .clr(rst));
  Register #(.trigger("falling"), .width(32)) x4 (.D(DataD), .en(AddrD_x4), .clk(clk), .Q(Data_x4), .clr(rst));
  Register #(.trigger("falling"), .width(32)) x5 (.D(DataD), .en(AddrD_x5), .clk(clk), .Q(Data_x5), .clr(rst));
  Register #(.trigger("falling"), .width(32)) x6 (.D(DataD), .en(AddrD_x6), .clk(clk), .Q(Data_x6), .clr(rst));
  Register #(.trigger("falling"), .width(32)) x7 (.D(DataD), .en(AddrD_x7), .clk(clk), .Q(Data_x7), .clr(rst));
  Register #(.trigger("falling"), .width(32)) x8 (.D(DataD), .en(AddrD_x8), .clk(clk), .Q(Data_x8), .clr(rst));
  Register #(.trigger("falling"), .width(32)) x9 (.D(DataD), .en(AddrD_x9), .clk(clk), .Q(Data_x9), .clr(rst));
  Register #(.trigger("falling"), .width(32)) x10 (.D(DataD), .en(AddrD_x10), .clk(clk), .Q(Data_x10), .clr(rst));
  Register #(.trigger("falling"), .width(32)) x11 (.D(DataD), .en(AddrD_x11), .clk(clk), .Q(Data_x11), .clr(rst));
  Register #(.trigger("falling"), .width(32)) x12 (.D(DataD), .en(AddrD_x12), .clk(clk), .Q(Data_x12), .clr(rst));
  Register #(.trigger("falling"), .width(32)) x13 (.D(DataD), .en(AddrD_x13), .clk(clk), .Q(Data_x13), .clr(rst));
  Register #(.trigger("falling"), .width(32)) x14 (.D(DataD), .en(AddrD_x14), .clk(clk), .Q(Data_x14), .clr(rst));
  Register #(.trigger("falling"), .width(32)) x15 (.D(DataD), .en(AddrD_x15), .clk(clk), .Q(Data_x15), .clr(rst));
  Register #(.trigger("falling"), .width(32)) x16 (.D(DataD), .en(AddrD_x16), .clk(clk), .Q(Data_x16), .clr(rst));
  Register #(.trigger("falling"), .width(32)) x17 (.D(DataD), .en(AddrD_x17), .clk(clk), .Q(Data_x17), .clr(rst));
  Register #(.trigger("falling"), .width(32)) x18 (.D(DataD), .en(AddrD_x18), .clk(clk), .Q(Data_x18), .clr(rst));
  Register #(.trigger("falling"), .width(32)) x19 (.D(DataD), .en(AddrD_x19), .clk(clk), .Q(Data_x19), .clr(rst));
  Register #(.trigger("falling"), .width(32)) x20 (.D(DataD), .en(AddrD_x20), .clk(clk), .Q(Data_x20), .clr(rst));
  Register #(.trigger("falling"), .width(32)) x21 (.D(DataD), .en(AddrD_x21), .clk(clk), .Q(Data_x21), .clr(rst));
  Register #(.trigger("falling"), .width(32)) x22 (.D(DataD), .en(AddrD_x22), .clk(clk), .Q(Data_x22), .clr(rst));
  Register #(.trigger("falling"), .width(32)) x23 (.D(DataD), .en(AddrD_x23), .clk(clk), .Q(Data_x23), .clr(rst));
  Register #(.trigger("falling"), .width(32)) x24 (.D(DataD), .en(AddrD_x24), .clk(clk), .Q(Data_x24), .clr(rst));
  Register #(.trigger("falling"), .width(32)) x25 (.D(DataD), .en(AddrD_x25), .clk(clk), .Q(Data_x25), .clr(rst));
  Register #(.trigger("falling"), .width(32)) x26 (.D(DataD), .en(AddrD_x26), .clk(clk), .Q(Data_x26), .clr(rst));
  Register #(.trigger("falling"), .width(32)) x27 (.D(DataD), .en(AddrD_x27), .clk(clk), .Q(Data_x27), .clr(rst));
  Register #(.trigger("falling"), .width(32)) x28 (.D(DataD), .en(AddrD_x28), .clk(clk), .Q(Data_x28), .clr(rst));
  Register #(.trigger("falling"), .width(32)) x29 (.D(DataD), .en(AddrD_x29), .clk(clk), .Q(Data_x29), .clr(rst));
  Register #(.trigger("falling"), .width(32)) x30 (.D(DataD), .en(AddrD_x30), .clk(clk), .Q(Data_x30), .clr(rst));
  Register #(.trigger("falling"), .width(32)) x31 (.D(DataD), .en(AddrD_x31), .clk(clk), .Q(Data_x31), .clr(rst));
  Multiplexer #(.select(5), .width(32)) multiplexer_1 (
    .in0(Data_x0), .in1(Data_x1), .in2(Data_x2), .in3(Data_x3), .in4(Data_x4), .in5(Data_x5), .in6(Data_x6),
    .in7(Data_x7), .in8(Data_x8), .in9(Data_x9), .in10(Data_x10), .in11(Data_x11), .in12(Data_x12),
    .in13(Data_x13), .in14(Data_x14), .in15(Data_x15), .in16(Data_x16), .in17(Data_x17), .in18(Data_x18),
    .in19(Data_x19), .in20(Data_x20), .in21(Data_x21), .in22(Data_x22), .in23(Data_x23), .in24(Data_x24),
    .in25(Data_x25), .in26(Data_x26), .in27(Data_x27), .in28(Data_x28), .in29(Data_x29), .in30(Data_x30),
    .in31(Data_x31), .out(DataA), .sel(AddrA));
  Multiplexer #(.select(5), .width(32)) multiplexer_2 (
    .in0(Data_x0), .in1(Data_x1), .in2(Data_x2), .in3(Data_x3), .in4(Data_x4), .in5(Data_x5), .in6(Data_x6),
    .in7(Data_x7), .in8(Data_x8), .in9(Data_x9), .in10(Data_x10), .in11(Data_x11), .in12(Data_x12),
    .in13(Data_x13), .in14(Data_x14), .in15(Data_x15), .in16(Data_x16), .in17(Data_x17), .in18(Data_x18),
    .in19(Data_x19), .in20(Data_x20), .in21(Data_x21), .in22(Data_x22), .in23(Data_x23), .in24(Data_x24),
    .in25(Data_x25), .in26(Data_x26), .in27(Data_x27), .in28(Data_x28), .in29(Data_x29), .in30(Data_x30),
    .in31(Data_x31), .out(DataB), .sel(AddrB));
endmodule
